# Fritzing sketch bai1+bai2 (saved by Fritzing 0.9.5d)
breadboards: 1

parts:
  LED1 = LED - 5mm [color="Red (633nm)" package="5 mm [THT]"]
  S1 = SWITCH-MOMENTARY-2 [package=tactile-pth-12mm]  # not connected
  S2 = SWITCH-MOMENTARY-2 [package=tactile-pth-12mm]  # not connected
  S3 = Pushbutton [package="[SMD]"]
  U1 = ESP32S-HiLetgo [part_number=ESP32S-HiLetgo]

nets:
  N1: LED1.cathode, S3.Pin_3, S3.Pin_4, U1.GND
  N2: LED1.anode, U1.GPIO2
  N3: S3.Pin_1, S3.Pin_2, U1.GPIO4

custom parts:
  ESP32S-HiLetgo: HiLetgo ESP-WROOM-32 ESP32 ESP-32S Development Board 2.4GHz Dual-Mode WiFi + Bluetooth Dual Cores Microcontroller The ESP32 integrated with Antenna switches, RF Balun, power amplifiers, low-noise amplifiers, filters, and management modules, and the entire solution occupies the least area of PCB. 2.4 GHz Wi-Fi plus Bluetooth dual-mode chip, with TSMC Ultra-low power consumption 40nm technology,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
